# Fritzing sketch sketch (saved by Fritzing 1.0.4)
circuit board: 9cm x 7cm
perfboards: 1

parts:
  Adafruit_Feather_RP2040_Adalogger1 = Adafruit Feather RP2040 Adalogger [part_number=#5980]
  WaveShare_1_3inch_OLED_128x1 = WaveShare 1.3inch OLED 128x64
  R2 = Resistor [tolerance=±5% power=0.25W resistance=51k package=THT]
  R3 = Resistor [tolerance=±5% power=0.25W resistance=51k package=THT]
  Adafruit_Ultimate_GPS_Breakout = Adafruit Ultimate GPS v3 [part_number="Adafruit #746"]
  2000mAh_LiPo = Lithium Ion Polymer Battery 3.7v 2000mAh [part_number=2011]
  Part1 = 24 NeoPixel Ring [part_number=1586]
  Part2 = Adafruit BNO085 9-DOF Orientation IMU Fusion [part_number="Addfruit #4754"]

nets:
  GND: Adafruit_Feather_RP2040_Adalogger1.GND, WaveShare_1_3inch_OLED_128x1.GND, WaveShare_1_3inch_OLED_128x1.D/C, R2.Pin_1, Adafruit_Ultimate_GPS_Breakout.GND, 2000mAh_LiPo.negative, Part1.GND, Part2.GND
  VCC: Adafruit_Feather_RP2040_Adalogger1.+3V3, WaveShare_1_3inch_OLED_128x1.VCC, Adafruit_Ultimate_GPS_Breakout.VIN, Part2.VCC
  N1: Adafruit_Feather_RP2040_Adalogger1.SCL, WaveShare_1_3inch_OLED_128x1.CLK
  N2: Adafruit_Feather_RP2040_Adalogger1.D4, Adafruit_Ultimate_GPS_Breakout.ENABLE
  N3: Adafruit_Feather_RP2040_Adalogger1.TX, Adafruit_Ultimate_GPS_Breakout.RX
  N4: Adafruit_Feather_RP2040_Adalogger1.RX, Adafruit_Ultimate_GPS_Breakout.TX
  N5: Adafruit_Feather_RP2040_Adalogger1.SCK, Part2.INT
  N6: Adafruit_Feather_RP2040_Adalogger1.D25, Part2.SCL/SCK/RX
  N7: Adafruit_Feather_RP2040_Adalogger1.D24, Part2.SDA/MISO/TX
  N8: Adafruit_Feather_RP2040_Adalogger1.A0, R2.Pin_0, R3.Pin_1
  N9: Adafruit_Feather_RP2040_Adalogger1.VBAT, R3.Pin_0, 2000mAh_LiPo.positive, Part1.VDD
  N10: Adafruit_Feather_RP2040_Adalogger1.D12, Part1.IN
  N11: Adafruit_Feather_RP2040_Adalogger1.D5, WaveShare_1_3inch_OLED_128x1.RES
  N12: Adafruit_Feather_RP2040_Adalogger1.SDA, WaveShare_1_3inch_OLED_128x1.DIN

custom parts:
  Adafruit Feather RP2040 Adalogger: This is the Adafruit Feather RP2040 Adalogger - our take on an 'all-in-one' RP2040 data-logger (or data-reader) with built-in USB, battery charging, and a microSD holder ready to rock! We have other boards in the Feather family, check'em out here The RP2040 Adalogger is the same size and shape as a Feather and is intended to make your next data logging or data reading project super easy. Micro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
  WaveShare 1.3inch OLED 128x64: OLED Original design by Simulz (http://tsblog.simulz.kr) Corrected PCB layout by Andreas Horneffer
  Adafruit Ultimate GPS v3: We carry a few different GPS modules here in the Adafruit shop, but none that satisfied our every desire - that's why we designed this little GPS breakout board. We believe this is the Ultimate GPS module, so we named it that. It's got everything you want and more: -165 dBm sensitivity, 10 Hz updates, 66 channels 5V friendly design and only 20mA current draw Breadboard friendly + two mounting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
  Lithium Ion Polymer Battery 3.7v 2000mAh: Lithium ion polymer (also known as 'lipo' or 'lipoly') batteries are thin, light and powerful. The output ranges from 4.2V when completely charged to 3.7V. This battery has a capacity of 2000mAh. The batteries come pre-attached with a genuine 2-pin JST-PH connector as shown and include the necessary protection circuitry.
  24 NeoPixel Ring: 24 ultra bright smart LED NeoPixels are arranged in a circle with 2.6" (66mm) outer diameter. The rings are 'chainable' - connect the output pin of one to the input pin of another. Use only one microcontroller pin to control as many as you can chain together! Each LED is addressable as the driver chip is inside the LED. Each one has ~18mA constant current drive so the color will be very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
